// Logisim project Proj2starter.circ as structural Verilog: 4 circuits, main circuit regfile
module CPUmain (
  input  [31:0] in_1
);

  wire control_1_alu_code, control_1_imm_sel, control_1_reg_write_e;
  wire [4:0] control_1_rd, control_1_rs, control_1_rt;
  wire [31:0] alu_1_res, control_1_imm, multiplexer_1_out, regfile_1_rs_data, regfile_1_rt_data;

  regfile regfile_1 (
    .write_e(control_1_reg_write_e), .rt(control_1_rt), .rd(control_1_rd), .rs(control_1_rs),
    .rd_data(alu_1_res), .rs_data(regfile_1_rs_data), .rt_data(regfile_1_rt_data));
  Control control_1 (
    .Inst(in_1), .rs(control_1_rs), .rt(control_1_rt), .rd(control_1_rd), .imm(control_1_imm),
    .reg_write_e(control_1_reg_write_e), .imm_sel(control_1_imm_sel), .ALU_code(control_1_alu_code));
  Multiplexer #(.width(32)) multiplexer_1 (
    .in0(regfile_1_rt_data), .in1(control_1_imm), .out(multiplexer_1_out), .sel(control_1_imm_sel));
  ALU alu_1 (.OP1(regfile_1_rs_data), .OP2(multiplexer_1_out), .ALU_CODE(control_1_alu_code), .Res(alu_1_res));
endmodule

module regfile (
  input  [4:0] rd,
  input  [4:0] rs,
  input  [4:0] rt,
  input  write_e,
  input  [31:0] rd_data,
  output [31:0] rs_data,
  output [31:0] rt_data
);

  wire clock_1_out, demultiplexer_1_out0, demultiplexer_1_out12, demultiplexer_1_out13,
       demultiplexer_1_out14, demultiplexer_1_out15, demultiplexer_1_out16, demultiplexer_1_out17,
       demultiplexer_1_out18, demultiplexer_1_out19, demultiplexer_1_out20, demultiplexer_1_out21,
       demultiplexer_1_out22, demultiplexer_1_out23, demultiplexer_1_out24, demultiplexer_1_out25,
       demultiplexer_1_out26, demultiplexer_1_out27, demultiplexer_1_out28, demultiplexer_1_out29,
       demultiplexer_1_out30, demultiplexer_1_out31, WE1, WE2, WE3, WE4, WE5, WE6, WE7, WE8, WE9, WE10, WE11;
  wire [31:0] a, r17, r18, r19, r20, r21, r22, r23, r24, r25, r26, r27, r28, r29, r30, r31, register_1_q,
       register_2_q, register_3_q, register_4_q, register_5_q, register_6_q, register_7_q, register_8_q,
       register_9_q, register_10_q, register_11_q, register_12_q, register_13_q, register_14_q,
       register_15_q, register_16_q;

  Demultiplexer #(.select(5)) demultiplexer_1 (
    .out0(demultiplexer_1_out0), .out1(WE1), .out2(WE2), .out3(WE3), .out4(WE4), .out5(WE5), .out6(WE6),
    .out7(WE7), .out8(WE8), .out9(WE9), .out10(WE10), .out11(WE11), .out12(demultiplexer_1_out12),
    .out13(demultiplexer_1_out13), .out14(demultiplexer_1_out14), .out15(demultiplexer_1_out15),
    .out16(demultiplexer_1_out16), .out17(demultiplexer_1_out17), .out18(demultiplexer_1_out18),
    .out19(demultiplexer_1_out19), .out20(demultiplexer_1_out20), .out21(demultiplexer_1_out21),
    .out22(demultiplexer_1_out22), .out23(demultiplexer_1_out23), .out24(demultiplexer_1_out24),
    .out25(demultiplexer_1_out25), .out26(demultiplexer_1_out26), .out27(demultiplexer_1_out27),
    .out28(demultiplexer_1_out28), .out29(demultiplexer_1_out29), .out30(demultiplexer_1_out30),
    .out31(demultiplexer_1_out31), .in(write_e), .sel(rd));
  Clock clock_1 (.out(clock_1_out));
  Register #(.width(32)) register_1 (.D({32{1'b0}}), .en(1'b0), .clk(clock_1_out), .Q(register_1_q));  // open: clr
  Register #(.width(32)) register_2 (.D(rd_data), .en(WE1), .clk(clock_1_out), .Q(register_2_q));  // open: clr
  Register #(.width(32)) register_3 (.D(rd_data), .en(WE2), .clk(clock_1_out), .Q(register_3_q));  // open: clr
  Register #(.width(32)) register_4 (.D(rd_data), .en(WE3), .clk(clock_1_out), .Q(register_4_q));  // open: clr
  Register #(.width(32)) register_5 (.D(rd_data), .en(WE4), .clk(clock_1_out), .Q(register_5_q));  // open: clr
  Register #(.width(32)) register_6 (.D(rd_data), .en(WE5), .clk(clock_1_out), .Q(register_6_q));  // open: clr
  Register #(.width(32)) register_7 (.D(rd_data), .en(WE6), .clk(clock_1_out), .Q(register_7_q));  // open: clr
  Register #(.width(32)) register_8 (.D(rd_data), .en(WE7), .clk(clock_1_out), .Q(register_8_q));  // open: clr
  Register #(.width(32)) register_9 (.D(rd_data), .en(WE8), .clk(clock_1_out), .Q(register_9_q));  // open: clr
  Register #(.width(32)) register_10 (.D(rd_data), .en(WE9), .clk(clock_1_out), .Q(register_10_q));  // open: clr
  Register #(.width(32)) register_11 (.D(rd_data), .en(WE10), .clk(clock_1_out), .Q(register_11_q));  // open: clr
  Register #(.width(32)) register_12 (.D(rd_data), .en(WE11), .clk(clock_1_out), .Q(register_12_q));  // open: clr
  Register #(.width(32)) register_13 (
    .D(rd_data), .en(demultiplexer_1_out12), .clk(clock_1_out), .Q(register_13_q));  // open: clr
  Register #(.width(32)) register_14 (
    .D(rd_data), .en(demultiplexer_1_out13), .clk(clock_1_out), .Q(register_14_q));  // open: clr
  Register #(.width(32)) register_15 (
    .D(rd_data), .en(demultiplexer_1_out14), .clk(clock_1_out), .Q(register_15_q));  // open: clr
  Register #(.width(32)) register_16 (
    .D(rd_data), .en(demultiplexer_1_out15), .clk(clock_1_out), .Q(register_16_q));  // open: clr
  Register #(.width(32)) register_17 (.D(rd_data), .en(demultiplexer_1_out16), .clk(clock_1_out), .Q(a));  // open: clr
  Register #(.width(32)) register_18 (
    .D(rd_data), .en(demultiplexer_1_out17), .clk(clock_1_out), .Q(r17));  // open: clr
  Register #(.width(32)) register_19 (
    .D(rd_data), .en(demultiplexer_1_out18), .clk(clock_1_out), .Q(r18));  // open: clr
  Register #(.width(32)) register_20 (
    .D(rd_data), .en(demultiplexer_1_out19), .clk(clock_1_out), .Q(r19));  // open: clr
  Register #(.width(32)) register_21 (
    .D(rd_data), .en(demultiplexer_1_out20), .clk(clock_1_out), .Q(r20));  // open: clr
  Register #(.width(32)) register_22 (
    .D(rd_data), .en(demultiplexer_1_out21), .clk(clock_1_out), .Q(r21));  // open: clr
  Register #(.width(32)) register_23 (
    .D(rd_data), .en(demultiplexer_1_out22), .clk(clock_1_out), .Q(r22));  // open: clr
  Register #(.width(32)) register_24 (
    .D(rd_data), .en(demultiplexer_1_out23), .clk(clock_1_out), .Q(r23));  // open: clr
  Register #(.width(32)) register_25 (
    .D(rd_data), .en(demultiplexer_1_out24), .clk(clock_1_out), .Q(r24));  // open: clr
  Register #(.width(32)) register_26 (
    .D(rd_data), .en(demultiplexer_1_out25), .clk(clock_1_out), .Q(r25));  // open: clr
  Register #(.width(32)) register_27 (
    .D(rd_data), .en(demultiplexer_1_out26), .clk(clock_1_out), .Q(r26));  // open: clr
  Register #(.width(32)) register_28 (
    .D(rd_data), .en(demultiplexer_1_out27), .clk(clock_1_out), .Q(r27));  // open: clr
  Register #(.width(32)) register_29 (
    .D(rd_data), .en(demultiplexer_1_out28), .clk(clock_1_out), .Q(r28));  // open: clr
  Register #(.width(32)) register_30 (
    .D(rd_data), .en(demultiplexer_1_out29), .clk(clock_1_out), .Q(r29));  // open: clr
  Register #(.width(32)) register_31 (
    .D(rd_data), .en(demultiplexer_1_out30), .clk(clock_1_out), .Q(r30));  // open: clr
  Register #(.width(32)) register_32 (
    .D(rd_data), .en(demultiplexer_1_out31), .clk(clock_1_out), .Q(r31));  // open: clr
  Multiplexer #(.select(5), .width(32)) multiplexer_1 (
    .in0(register_1_q), .in1(register_2_q), .in2(register_3_q), .in3(register_4_q), .in4(register_5_q),
    .in5(register_6_q), .in6(register_7_q), .in7(register_8_q), .in8(register_9_q), .in9(register_10_q),
    .in10(register_11_q), .in11(register_12_q), .in12(register_13_q), .in13(register_14_q),
    .in14(register_15_q), .in15(register_16_q), .in16(a), .in17(r17), .in18(r18), .in19(r19), .in20(r20),
    .in21(r21), .in22(r22), .in23(r23), .in24(r24), .in25(r25), .in26(r26), .in27(r27), .in28(r28),
    .in29(r29), .in30(r30), .in31(r31), .out(rs_data), .sel(rs));
  Multiplexer #(.select(5), .width(32)) multiplexer_2 (
    .in0(register_1_q), .in1(register_2_q), .in2(register_3_q), .in3(register_4_q), .in4(register_5_q),
    .in5(register_6_q), .in6(register_7_q), .in7(register_8_q), .in8(register_9_q), .in9(register_10_q),
    .in10(register_11_q), .in11(register_12_q), .in12(register_13_q), .in13(register_14_q),
    .in14(register_15_q), .in15(register_16_q), .in16(a), .in17(r17), .in18(r18), .in19(r19), .in20(r20),
    .in21(r21), .in22(r22), .in23(r23), .in24(r24), .in25(r25), .in26(r26), .in27(r27), .in28(r28),
    .in29(r29), .in30(r30), .in31(r31), .out(rt_data), .sel(rt));

  // Other names for the same wires on the sheet: multRS[31:0] = rs_data; multRT[31:0] = rt_data; r16[31:0] = a;
  //   WE_IN = write_e
endmodule

module ALU (
  input  ALU_CODE,
  input  [31:0] OP1,
  input  [31:0] OP2,
  output [31:0] Res
);

  Adder adder_1 ();  // open: a, b, out, cin, cout
  Subtractor subtractor_1 ();  // open: a, b, out, bin, bout
  Multiplier multiplier_1 ();  // open: a, b, out, cin, cout
  Divider divider_1 ();  // open: a, b, out, upper, rem
  Comparator comparator_1 ();  // open: a, b, gt, eq, lt
  Shifter shifter_1 ();  // open: in, dist, out
  Shifter #(.shift("lr")) shifter_2 ();  // open: in, dist, out
  Register HI ();  // open: D, en, clk, Q, clr
  Register LO ();  // open: D, en, clk, Q, clr
endmodule

module Control (
  input  [31:0] Inst,
  output [4:0] rs,
  output [4:0] rt,
  output [4:0] rd,
  output [31:0] imm,
  output reg_write_e,
  output imm_sel,
  output ALU_code
);
endmodule
