// Logisim project ProjectBusLayout.circ as structural Verilog: 16 circuits, main circuit Computer
module Computer (
);

  wire buzzercontroller_1_buzzeron, clock_1_out, clock_2_out, clock_3_out, cpu_1_buswriteenable,
       joystickcontroller_1_writetobus, keyboard_1_avail, keyboardcontroller_1_keyboardread,
       keyboardcontroller_1_writetobus, memorycontroller_1_writeenabletomem, memorycontroller_1_writetobus,
       rgb_video_1_p1, rgb_video_1_p2, rgb_video_1_p3, slidercontroller_1_writetobus,
       terminalcontroller_1_writetoterminal;
  wire [3:0] joystick_1_x, joystick_1_y, ledhexcontroller_1_datatoled;
  wire [6:0] buzzercontroller_1_volout, keyboard_1_data, terminalcontroller_1_datatoterminal;
  wire [7:0] buzzercontroller_1_dutycycleout, rgb_video_1_p4, rgb_video_1_p5, slider_1_out;
  wire [13:0] buzzercontroller_1_freqout;
  wire [23:0] memorycontroller_1_addresstomem, rgb_video_1_p6;
  wire [31:0] controlled_buffer_1_out, cpu_1_addresstobus, cpu_1_datatobus, joystickcontroller_1_datatobus,
       keyboardcontroller_1_datatobus, memorycontroller_1_datatobus, memorycontroller_1_datatomem,
       ram_1_dout, slidercontroller_1_datatobus;

  RAM #(.addrWidth(24), .dataWidth(32), .enables("line")) ram_1 (
    .addr(memorycontroller_1_addresstomem), .we(memorycontroller_1_writeenabletomem), .clk(clock_1_out),
    .din(memorycontroller_1_datatomem), .dout(ram_1_dout));
  Clock clock_1 (.out(clock_1_out));
  Slider slider_1 (.out(slider_1_out));
  Clock clock_2 (.out(clock_2_out));
  Keyboard keyboard_1 (
    .clk(clock_2_out), .re(keyboardcontroller_1_keyboardread), .avail(keyboard_1_avail),
    .data(keyboard_1_data));  // open: clr
  MemoryController memorycontroller_1 (
    .WriteEnableFromBus(cpu_1_buswriteenable), .AddressFromBus(cpu_1_addresstobus), .DataFromMem(ram_1_dout),
    .DataFromBus(controlled_buffer_1_out), .WriteEnableToMem(memorycontroller_1_writeenabletomem),
    .DataToBus(memorycontroller_1_datatobus), .AddressToMem(memorycontroller_1_addresstomem),
    .DataToMem(memorycontroller_1_datatomem), .WriteToBus(memorycontroller_1_writetobus));
  CPU cpu_1 (
    .DataFromBus(controlled_buffer_1_out), .BusWriteEnable(cpu_1_buswriteenable),
    .DataToBus(cpu_1_datatobus), .AddressToBus(cpu_1_addresstobus));
  // Probe on cpu_1_addresstobus
  SliderController slidercontroller_1 (
    .WriteEnableFromBus(cpu_1_buswriteenable), .AddressFromBus(cpu_1_addresstobus),
    .SliderData(slider_1_out), .WriteToBus(slidercontroller_1_writetobus),
    .DataToBus(slidercontroller_1_datatobus));
  // Probe on controlled_buffer_1_out
  assign controlled_buffer_1_out = memorycontroller_1_writetobus ? memorycontroller_1_datatobus : 32'bz;  // Controlled_Buffer controlled_buffer_1
  // Probe on controlled_buffer_1_out
  assign controlled_buffer_1_out = cpu_1_buswriteenable ? cpu_1_datatobus : 32'bz;  // Controlled_Buffer controlled_buffer_2
  // Probe on controlled_buffer_1_out
  KeyboardController keyboardcontroller_1 (
    .DataFromBus(controlled_buffer_1_out), .WriteEnableFromBus(cpu_1_buswriteenable),
    .AddressFromBus(cpu_1_addresstobus), .KeyboardData(keyboard_1_data), .KeyboardStatus(keyboard_1_avail),
    .DataToBus(keyboardcontroller_1_datatobus), .KeyboardRead(keyboardcontroller_1_keyboardread),
    .WriteToBus(keyboardcontroller_1_writetobus));
  assign controlled_buffer_1_out = keyboardcontroller_1_writetobus ? keyboardcontroller_1_datatobus : 32'bz;  // Controlled_Buffer controlled_buffer_3
  assign controlled_buffer_1_out = slidercontroller_1_writetobus ? slidercontroller_1_datatobus : 32'bz;  // Controlled_Buffer controlled_buffer_4
  Clock clock_3 (.out(clock_3_out));
  TTY tty_1 (
    .data(terminalcontroller_1_datatoterminal), .clk(clock_3_out), .we(terminalcontroller_1_writetoterminal));  // open: clr
  // RGB_Video #(.height(256), .scale(1), .width(256)) rgb_video_1: pin names not known; wires that end beside it: rgb_video_1_p1, rgb_video_1_p2, rgb_video_1_p3, rgb_video_1_p4, rgb_video_1_p5, rgb_video_1_p6
  Clock clock_4 (.out(rgb_video_1_p2));
  Joystick joystick_1 (.x(joystick_1_x), .y(joystick_1_y));
  // Probe on joystick_1_y
  TerminalController terminalcontroller_1 (
    .WriteEnableFromBus(cpu_1_buswriteenable), .AddressFromBus(cpu_1_addresstobus),
    .DataFromBus(controlled_buffer_1_out), .DataToTerminal(terminalcontroller_1_datatoterminal),
    .WriteToTerminal(terminalcontroller_1_writetoterminal));
  RGBController rgbcontroller_1 (
    .AddressFromBus(cpu_1_addresstobus), .DataFromBus(controlled_buffer_1_out),
    .WriteEnable(cpu_1_buswriteenable), .RGBX(rgb_video_1_p4), .RGBY(rgb_video_1_p5),
    .RGBColor(rgb_video_1_p6), .RGBWrite(rgb_video_1_p3), .resetScreen(rgb_video_1_p1));
  LEDHexController ledhexcontroller_1 (
    .WriteEnableFromBus(cpu_1_buswriteenable), .AddressFromBus(cpu_1_addresstobus),
    .DataFromBus(controlled_buffer_1_out), .DataToLED(ledhexcontroller_1_datatoled));
  // Probe on rgb_video_1_p4
  // Probe on rgb_video_1_p5
  JoyStickController joystickcontroller_1 (
    .DataFromBus(controlled_buffer_1_out), .WriteEnableFromBus(cpu_1_buswriteenable),
    .AddressFromBus(cpu_1_addresstobus), .JoyStickDataX(joystick_1_x), .JoyStickDataY(joystick_1_y),
    .WriteToBus(joystickcontroller_1_writetobus), .DataToBus(joystickcontroller_1_datatobus));
  BuzzerController buzzercontroller_1 (
    .AddressFromBus(cpu_1_addresstobus), .DataFromBus(controlled_buffer_1_out),
    .WriteEnable(cpu_1_buswriteenable), .VolOut(buzzercontroller_1_volout),
    .FreqOut(buzzercontroller_1_freqout), .DutyCycleOut(buzzercontroller_1_dutycycleout),
    .BuzzerOn(buzzercontroller_1_buzzeron));
  assign controlled_buffer_1_out = joystickcontroller_1_writetobus ? joystickcontroller_1_datatobus : 32'bz;  // Controlled_Buffer controlled_buffer_5
  Hex_Digit_Display hex_digit_display_1 (.value(ledhexcontroller_1_datatoled));  // open: dp
  // Buzzer buzzer_1: pin names not known; wires that end beside it: buzzercontroller_1_freqout, buzzercontroller_1_buzzeron, buzzercontroller_1_volout, buzzercontroller_1_dutycycleout

  // Notes on the sheet:
  //   Write_enable
  //   Address
  //   Data
endmodule

module CPU (
  input  [31:0] DataFromBus,
  output [31:0] AddressToBus,
  output BusWriteEnable,
  output [31:0] DataToBus
);

  wire branchcheck_1_isbranch, clock_1_out, comparator_1_eq, control_1_alljumpselect,
       control_1_dataoutplexer, control_1_imm_sel, control_1_jalrjalsignal, control_1_jumpjalselect,
       control_1_reg_write_e;
  wire [4:0] control_1_alu_code, control_1_rd, control_1_rs, control_1_rt;
  wire [5:0] bit_extender_4_out;
  wire [23:0] bit_extender_3_out;
  wire [25:0] bit_extender_1_out;
  wire [31:0] adder_1_out, adder_2_out, adder_3_out, bit_extender_2_out, control_1_imm, MemROM_data,
       multiplexer_1_out, multiplexer_2_out, multiplexer_3_out, multiplexer_4_out, multiplexer_5_out,
       multiplexer_6_out, PC_q, regfile_1_rs_data, shifter_1_out, shifter_2_out, shifter_3_out, shifter_4_out;

  Adder #(.width(32)) adder_1 (.a(32'h4), .b(PC_q), .out(adder_1_out));  // open: cin, cout
  Shifter #(.width(32)) shifter_1 (.in(control_1_imm), .\dist (5'b00010), .out(shifter_1_out));
  Adder #(.width(32)) adder_2 (.a(adder_1_out), .b(shifter_1_out), .out(adder_2_out));  // open: cin, cout
  Multiplexer #(.width(32)) multiplexer_1 (
    .in0(adder_1_out), .in1(adder_2_out), .out(multiplexer_1_out), .sel(branchcheck_1_isbranch));
  Register #(.width(32)) PC (.D(multiplexer_3_out), .en(1'b1), .clk(clock_1_out), .Q(PC_q));  // open: clr
  Clock clock_1 (.out(clock_1_out));
  Multiplexer #(.width(32)) multiplexer_2 (
    .in0(regfile_1_rs_data), .in1(shifter_2_out), .out(multiplexer_2_out), .sel(control_1_jumpjalselect));
  Shifter #(.width(32)) shifter_2 (.in(bit_extender_2_out), .\dist (5'b00010), .out(shifter_2_out));
  Bit_Extender #(.in_width(32), .out_width(26), .\type ("zero")) bit_extender_1 (
    .in(MemROM_data), .out(bit_extender_1_out));
  Multiplexer #(.width(32)) multiplexer_3 (
    .in0(multiplexer_1_out), .in1(multiplexer_2_out), .out(multiplexer_3_out), .sel(control_1_alljumpselect));
  assign bit_extender_2_out = {{6{1'b0}}, bit_extender_1_out};  // Bit_Extender bit_extender_2
  Shifter #(.shift("lr"), .width(32)) shifter_3 (.in(PC_q), .\dist (5'b00010), .out(shifter_3_out));
  ROM #(.addrWidth(24), .dataWidth(32)) MemROM (.addr(bit_extender_3_out), .data(MemROM_data));
  Bit_Extender #(.in_width(32), .out_width(24), .\type ("zero")) bit_extender_3 (
    .in(shifter_3_out), .out(bit_extender_3_out));
  Adder #(.width(32)) adder_3 (.a(PC_q), .b(32'h4), .out(adder_3_out));  // open: cin, cout
  Multiplexer #(.width(32)) multiplexer_4 (
    .in0(multiplexer_6_out), .in1(adder_3_out), .out(multiplexer_4_out), .sel(control_1_jalrjalsignal));
  // Probe on control_1_rd
  // Probe on control_1_rs
  regfile regfile_1 (
    .write_e(control_1_reg_write_e), .rt(control_1_rt), .rd(control_1_rd), .rs(control_1_rs),
    .rd_data(multiplexer_4_out), .rs_data(regfile_1_rs_data), .rt_data(DataToBus));
  // Probe on control_1_rt
  Control control_1 (
    .Inst(MemROM_data), .imm_sel(control_1_imm_sel), .rd(control_1_rd), .rs(control_1_rs),
    .imm(control_1_imm), .reg_write_e(control_1_reg_write_e), .ALU_code(control_1_alu_code),
    .rt(control_1_rt), .MemWE(BusWriteEnable), .DataOutPlexer(control_1_dataoutplexer),
    .JALRJALSignal(control_1_jalrjalsignal), .ALLJUMPSelect(control_1_alljumpselect),
    .JumpJALSelect(control_1_jumpjalselect));
  Multiplexer #(.width(32)) multiplexer_5 (
    .in0(DataToBus), .in1(control_1_imm), .out(multiplexer_5_out), .sel(control_1_imm_sel));
  Comparator #(.width(32)) comparator_1 (.a(regfile_1_rs_data), .b(DataToBus), .eq(comparator_1_eq));  // open: gt, lt
  Multiplexer #(.width(32)) multiplexer_6 (
    .in0(AddressToBus), .in1(DataFromBus), .out(multiplexer_6_out), .sel(control_1_dataoutplexer));
  Shifter #(.shift("lr"), .width(32)) shifter_4 (.in(MemROM_data), .\dist (5'b11010), .out(shifter_4_out));
  Bit_Extender #(.in_width(32), .out_width(6), .\type ("zero")) bit_extender_4 (
    .in(shifter_4_out), .out(bit_extender_4_out));
  ALU alu_1 (.OP2(multiplexer_5_out), .ALU_CODE(control_1_alu_code), .OP1(regfile_1_rs_data), .Res(AddressToBus));
  BranchCheck branchcheck_1 (.Opcode(bit_extender_4_out), .isEqual(comparator_1_eq), .IsBranch(branchcheck_1_isbranch));

  // Notes on the sheet:
  //   Normal PC
  //   Also decide which branch it is and convert output if neded
  //   BEQ,BNE
  //   Branches, adds offset, to PC+4
  //   jalr/jr
  //   Probably fixed
  //   Jump/jal
  //   Condition met? but doesnt actually go
  //   Errror at the point where we beq to   beq $t2, $zero, firstcalldone 
  //   Issue with assembler assigning the offset to FirstCalldone as 3?
  //   Offset for branches
  //   converts from byte to word addressed
  //   If any of the j type instructions, use bottom wire for PC
  //   contents of MemROM (hex, n*v repeats v):
  //   201b0000 105b000d 201b0001 105b0011 201b0005 105b0027 201b0009 105b003d 201b000a 105b0042 201b000b
  //   105b0041 201b000c 105b0043 3400008 3c1d03ff 201b01a0 3c1a03ff 375af000 af5b0000 800005c 10800012
  //   23bdffd8 3a01020 201b000a 9b001a d810 2012 237b0030 ac5b0000 20420004 1480fff8 3c1bffff 377bf000
  //   2042fffc 8c440000 af640000 145dfffc 23bd0028 3400008 3c1bffff 377bf000 20020030 af620000 3400008
  //   20020000 3c1bffff 377bf010 8f7b0000 1360fffc 3c1bffff 377bf014 8f7b0000 20070030 367382a 14e0000c
  //   2007003a 367382a 10e00009 237bffd0 2007000a 470018 1012 5b1020 3c1bffff 377bf010 af600000 800002e
  //   3400008 3c1b03ff 377bf000 8f620000 441020 af620000 441022 3400008 800004c 3c1bffff 377bf000 af640000
  //   3400008 3c1bffff 377bf010 8f7b0000 1360fffc 3c1bffff 377bf014 8f620000 3c1bffff 377bf010 af600000
  //   3400008 c0000be 800005e 2002000c d00c 25020 20080190 8d100000 20080194 8d110000 109020 119820
  //   200b0077 114b0007 200b0073 114b0007 200b0061 114b0007 200b0064 114b0007 800005e 2273ffff 8000077
  //   22730001 8000077 2252ffff 8000077 22520001 240782a 15e0ffe5 2008000a 248782a 11e0ffe2 260782a
  //   15e0ffe0 268782a 11e0ffde 1348c0 137840 12f4820 1324820 20080000 94880 1094020 8d090000 1120ffd5
  //   20080190 20090198 8d0a0000 ad2a0000 ad120000 20080194 2009019c 8d0a0000 ad2a0000 ad130000 3c0effff
  //   35cef020 20080190 8d090000 200a0194 8d4b0000 94880 21290064 b5880 216b0064 200c00ff c0000ab 20080198
  //   8d090000 200a019c 8d4b0000 94880 21290064 b5880 216b0064 3c0c0000 358c5500 c0000ab 800005e 120c020
  //   160c820 20140000 200f0004 128f000d 20150000 200f0004 12af0008 3154020 3344820 adc80000 adc90004
  //   adcc0008 adc0000c 22b50001 80000b1 22940001 80000ae 3e00008 1fb020 3c0effff 35cef020 200c0190
  //   8d8c0000 200d0194 8dad0000 20080000 200f000a 110f002c 20090000 200f000a 112f0027 3c040000 34845500
  //   152c0003 150d0002 200400ff 80000dc 850c0 85840 14b5020 1495020 200b0000 a5080 16a5820 8d6a0000
  //   15400002 3c0400aa 3484aaaa 95080 214a0064 85880 216b0064 20150000 200f0004 12af000d 20140000
  //   200f0004 128f0008 1547820 adcf0000 1757820 adcf0004 adc40008 adc0000c 22940001 80000e4 22b50001
  //   80000e1 21290001 80000c9 21080001 80000c6 16f820 3e00008
  //   Branch select not needed from control due to method of plexer cirucit 
  //   deciding when we store pc
  //   Need control switch to control thiis plexer
  //   Not sure what type of extender
endmodule

module MemoryController (
  input  WriteEnableFromBus,
  input  [31:0] AddressFromBus,
  input  [31:0] DataFromBus,
  input  [31:0] DataFromMem,
  output [31:0] DataToBus,
  output WriteToBus,
  output WriteEnableToMem,
  output [23:0] AddressToMem,
  output [31:0] DataToMem
);

  wire comparator_1_lt, not_1_out;
  wire [23:0] bit_extender_1_out;

  Comparator #(.mode("unsigned"), .width(32)) comparator_1 (
    .a(AddressFromBus), .b(32'h4000000), .lt(comparator_1_lt));  // open: gt, eq
  Bit_Extender #(.in_width(32), .out_width(24), .\type ("zero")) bit_extender_1 (
    .in(AddressFromBus), .out(bit_extender_1_out));
  not not_1 (not_1_out, WriteEnableFromBus);
  and and_1 (WriteEnableToMem, comparator_1_lt, WriteEnableFromBus);
  Shifter #(.shift("lr"), .width(24)) shifter_1 (.in(bit_extender_1_out), .\dist (5'b00010), .out(AddressToMem));
  and and_2 (WriteToBus, not_1_out, comparator_1_lt);

  assign DataToBus = DataFromMem;
  assign DataToMem = DataFromBus;
endmodule

module KeyboardController (
  input  [31:0] DataFromBus,
  input  WriteEnableFromBus,
  input  [31:0] AddressFromBus,
  input  [6:0] KeyboardData,
  input  KeyboardStatus,
  output WriteToBus,
  output [31:0] DataToBus,
  output KeyboardRead
);

  wire comparator_1_eq, comparator_2_eq, not_1_out, or_1_out;
  wire [31:0] bit_extender_1_out, bit_extender_2_out;

  not not_1 (not_1_out, WriteEnableFromBus);
  assign bit_extender_1_out = {{31{1'b0}}, KeyboardStatus};  // Bit_Extender bit_extender_1
  Comparator #(.mode("unsigned"), .width(32)) comparator_1 (
    .a(AddressFromBus), .b(32'hfffff014), .eq(comparator_1_eq));  // open: gt, lt
  Comparator #(.mode("unsigned"), .width(32)) comparator_2 (
    .a(AddressFromBus), .b(32'hfffff010), .eq(comparator_2_eq));  // open: gt, lt
  or or_1 (or_1_out, comparator_1_eq, comparator_2_eq);
  assign bit_extender_2_out = {{25{1'b0}}, KeyboardData};  // Bit_Extender bit_extender_2
  Multiplexer #(.width(32)) multiplexer_1 (
    .in0(bit_extender_2_out), .in1(bit_extender_1_out), .out(DataToBus), .sel(KeyboardRead));
  and and_1 (KeyboardRead, comparator_2_eq, WriteEnableFromBus);
  and and_2 (WriteToBus, or_1_out, not_1_out);
endmodule

module RGBController (
  input  [31:0] AddressFromBus,
  input  [31:0] DataFromBus,
  input  WriteEnable,
  output [7:0] RGBX,
  output [7:0] RGBY,
  output [23:0] RGBColor,
  output RGBWrite,
  output resetScreen
);

  wire and_1_out, and_2_out, and_3_out, clock_1_out, comparator_1_eq, comparator_2_eq, comparator_3_eq,
       comparator_4_eq, comparator_5_eq, not_1_out;
  wire [7:0] bit_extender_1_out;
  wire [23:0] bit_extender_2_out;

  Bit_Extender #(.in_width(32), .out_width(8), .\type ("zero")) bit_extender_1 (
    .in(DataFromBus), .out(bit_extender_1_out));
  Bit_Extender #(.in_width(32), .out_width(24), .\type ("zero")) bit_extender_2 (
    .in(DataFromBus), .out(bit_extender_2_out));
  Comparator #(.mode("unsigned"), .width(32)) comparator_1 (
    .a(AddressFromBus), .b(32'hfffff020), .eq(comparator_1_eq));  // open: gt, lt
  Comparator #(.mode("unsigned"), .width(32)) comparator_2 (
    .a(AddressFromBus), .b(32'hfffff024), .eq(comparator_2_eq));  // open: gt, lt
  Comparator #(.mode("unsigned"), .width(32)) comparator_3 (
    .a(AddressFromBus), .b(32'hfffff028), .eq(comparator_3_eq));  // open: gt, lt
  Comparator #(.mode("unsigned"), .width(32)) comparator_4 (
    .a(AddressFromBus), .b(32'hfffff02c), .eq(comparator_4_eq));  // open: gt, lt
  Comparator #(.mode("unsigned"), .width(32)) comparator_5 (
    .a(AddressFromBus), .b(32'hfffff050), .eq(comparator_5_eq));  // open: gt, lt
  not not_1 (not_1_out, WriteEnable);
  Clock clock_1 (.out(clock_1_out));
  and and_1 (and_1_out, WriteEnable, comparator_1_eq);
  and and_2 (and_2_out, WriteEnable, comparator_2_eq);
  and and_3 (and_3_out, WriteEnable, comparator_3_eq);
  and and_4 (RGBWrite, WriteEnable, comparator_4_eq);
  and and_5 (resetScreen, not_1_out, comparator_5_eq);
  Register XCord (.D(bit_extender_1_out), .en(and_1_out), .clk(clock_1_out), .Q(RGBX));  // open: clr
  Register YCord (.D(bit_extender_1_out), .en(and_2_out), .clk(clock_1_out), .Q(RGBY));  // open: clr
  Register #(.width(24)) RGB (.D(bit_extender_2_out), .en(and_3_out), .clk(clock_1_out), .Q(RGBColor));  // open: clr
endmodule

module TerminalController (
  input  WriteEnableFromBus,
  input  [31:0] AddressFromBus,
  input  [31:0] DataFromBus,
  output [6:0] DataToTerminal,
  output WriteToTerminal
);

  wire comparator_1_eq;

  Bit_Extender #(.in_width(32), .out_width(7), .\type ("zero")) bit_extender_1 (.in(DataFromBus), .out(DataToTerminal));
  Comparator #(.mode("unsigned"), .width(32)) comparator_1 (
    .a(AddressFromBus), .b(32'hfffff000), .eq(comparator_1_eq));  // open: gt, lt
  and and_1 (WriteToTerminal, WriteEnableFromBus, comparator_1_eq);
endmodule

module regfile (
  input  [4:0] rd,
  input  [4:0] rs,
  input  [4:0] rt,
  input  write_e,
  input  [31:0] rd_data,
  output [31:0] rs_data,
  output [31:0] rt_data
);

  wire clock_1_out, demultiplexer_1_out0, demultiplexer_1_out12, demultiplexer_1_out13,
       demultiplexer_1_out14, demultiplexer_1_out15, demultiplexer_1_out16, demultiplexer_1_out17,
       demultiplexer_1_out18, demultiplexer_1_out19, demultiplexer_1_out20, demultiplexer_1_out21,
       demultiplexer_1_out22, demultiplexer_1_out23, demultiplexer_1_out24, demultiplexer_1_out25,
       demultiplexer_1_out26, demultiplexer_1_out27, demultiplexer_1_out28, demultiplexer_1_out29,
       demultiplexer_1_out30, demultiplexer_1_out31, WE1, WE2, WE3, WE4, WE5, WE6, WE7, WE8, WE9, WE10, WE11;
  wire [31:0] a, r17, r18, r19, r20, r21, r22, r23, r24, r25, r26, r27, r28, r29, r30, r31, register_1_q,
       register_2_q, register_3_q, register_4_q, register_5_q, register_6_q, register_7_q, register_8_q,
       register_9_q, register_10_q, register_11_q, register_12_q, register_13_q, register_14_q,
       register_15_q, register_16_q;

  Demultiplexer #(.select(5)) demultiplexer_1 (
    .out0(demultiplexer_1_out0), .out1(WE1), .out2(WE2), .out3(WE3), .out4(WE4), .out5(WE5), .out6(WE6),
    .out7(WE7), .out8(WE8), .out9(WE9), .out10(WE10), .out11(WE11), .out12(demultiplexer_1_out12),
    .out13(demultiplexer_1_out13), .out14(demultiplexer_1_out14), .out15(demultiplexer_1_out15),
    .out16(demultiplexer_1_out16), .out17(demultiplexer_1_out17), .out18(demultiplexer_1_out18),
    .out19(demultiplexer_1_out19), .out20(demultiplexer_1_out20), .out21(demultiplexer_1_out21),
    .out22(demultiplexer_1_out22), .out23(demultiplexer_1_out23), .out24(demultiplexer_1_out24),
    .out25(demultiplexer_1_out25), .out26(demultiplexer_1_out26), .out27(demultiplexer_1_out27),
    .out28(demultiplexer_1_out28), .out29(demultiplexer_1_out29), .out30(demultiplexer_1_out30),
    .out31(demultiplexer_1_out31), .in(write_e), .sel(rd));
  Clock clock_1 (.out(clock_1_out));
  Register #(.width(32)) register_1 (.D({32{1'b0}}), .en(1'b0), .clk(clock_1_out), .Q(register_1_q));  // open: clr
  Register #(.width(32)) register_2 (.D(rd_data), .en(WE1), .clk(clock_1_out), .Q(register_2_q));  // open: clr
  Register #(.width(32)) register_3 (.D(rd_data), .en(WE2), .clk(clock_1_out), .Q(register_3_q));  // open: clr
  Register #(.width(32)) register_4 (.D(rd_data), .en(WE3), .clk(clock_1_out), .Q(register_4_q));  // open: clr
  Register #(.width(32)) register_5 (.D(rd_data), .en(WE4), .clk(clock_1_out), .Q(register_5_q));  // open: clr
  Register #(.width(32)) register_6 (.D(rd_data), .en(WE5), .clk(clock_1_out), .Q(register_6_q));  // open: clr
  Register #(.width(32)) register_7 (.D(rd_data), .en(WE6), .clk(clock_1_out), .Q(register_7_q));  // open: clr
  Register #(.width(32)) register_8 (.D(rd_data), .en(WE7), .clk(clock_1_out), .Q(register_8_q));  // open: clr
  Register #(.width(32)) register_9 (.D(rd_data), .en(WE8), .clk(clock_1_out), .Q(register_9_q));  // open: clr
  Register #(.width(32)) register_10 (.D(rd_data), .en(WE9), .clk(clock_1_out), .Q(register_10_q));  // open: clr
  Register #(.width(32)) register_11 (.D(rd_data), .en(WE10), .clk(clock_1_out), .Q(register_11_q));  // open: clr
  Register #(.width(32)) register_12 (.D(rd_data), .en(WE11), .clk(clock_1_out), .Q(register_12_q));  // open: clr
  Register #(.width(32)) register_13 (
    .D(rd_data), .en(demultiplexer_1_out12), .clk(clock_1_out), .Q(register_13_q));  // open: clr
  Register #(.width(32)) register_14 (
    .D(rd_data), .en(demultiplexer_1_out13), .clk(clock_1_out), .Q(register_14_q));  // open: clr
  Register #(.width(32)) register_15 (
    .D(rd_data), .en(demultiplexer_1_out14), .clk(clock_1_out), .Q(register_15_q));  // open: clr
  Register #(.width(32)) register_16 (
    .D(rd_data), .en(demultiplexer_1_out15), .clk(clock_1_out), .Q(register_16_q));  // open: clr
  Register #(.width(32)) register_17 (.D(rd_data), .en(demultiplexer_1_out16), .clk(clock_1_out), .Q(a));  // open: clr
  Register #(.width(32)) register_18 (
    .D(rd_data), .en(demultiplexer_1_out17), .clk(clock_1_out), .Q(r17));  // open: clr
  Register #(.width(32)) register_19 (
    .D(rd_data), .en(demultiplexer_1_out18), .clk(clock_1_out), .Q(r18));  // open: clr
  Register #(.width(32)) register_20 (
    .D(rd_data), .en(demultiplexer_1_out19), .clk(clock_1_out), .Q(r19));  // open: clr
  Register #(.width(32)) register_21 (
    .D(rd_data), .en(demultiplexer_1_out20), .clk(clock_1_out), .Q(r20));  // open: clr
  Register #(.width(32)) register_22 (
    .D(rd_data), .en(demultiplexer_1_out21), .clk(clock_1_out), .Q(r21));  // open: clr
  Register #(.width(32)) register_23 (
    .D(rd_data), .en(demultiplexer_1_out22), .clk(clock_1_out), .Q(r22));  // open: clr
  Register #(.width(32)) register_24 (
    .D(rd_data), .en(demultiplexer_1_out23), .clk(clock_1_out), .Q(r23));  // open: clr
  Register #(.width(32)) register_25 (
    .D(rd_data), .en(demultiplexer_1_out24), .clk(clock_1_out), .Q(r24));  // open: clr
  Register #(.width(32)) register_26 (
    .D(rd_data), .en(demultiplexer_1_out25), .clk(clock_1_out), .Q(r25));  // open: clr
  Register #(.width(32)) register_27 (
    .D(rd_data), .en(demultiplexer_1_out26), .clk(clock_1_out), .Q(r26));  // open: clr
  Register #(.width(32)) register_28 (
    .D(rd_data), .en(demultiplexer_1_out27), .clk(clock_1_out), .Q(r27));  // open: clr
  Register #(.width(32)) register_29 (
    .D(rd_data), .en(demultiplexer_1_out28), .clk(clock_1_out), .Q(r28));  // open: clr
  Register #(.width(32)) register_30 (
    .D(rd_data), .en(demultiplexer_1_out29), .clk(clock_1_out), .Q(r29));  // open: clr
  Register #(.width(32)) register_31 (
    .D(rd_data), .en(demultiplexer_1_out30), .clk(clock_1_out), .Q(r30));  // open: clr
  Register #(.width(32)) register_32 (
    .D(rd_data), .en(demultiplexer_1_out31), .clk(clock_1_out), .Q(r31));  // open: clr
  Multiplexer #(.select(5), .width(32)) multiplexer_1 (
    .in0(register_1_q), .in1(register_2_q), .in2(register_3_q), .in3(register_4_q), .in4(register_5_q),
    .in5(register_6_q), .in6(register_7_q), .in7(register_8_q), .in8(register_9_q), .in9(register_10_q),
    .in10(register_11_q), .in11(register_12_q), .in12(register_13_q), .in13(register_14_q),
    .in14(register_15_q), .in15(register_16_q), .in16(a), .in17(r17), .in18(r18), .in19(r19), .in20(r20),
    .in21(r21), .in22(r22), .in23(r23), .in24(r24), .in25(r25), .in26(r26), .in27(r27), .in28(r28),
    .in29(r29), .in30(r30), .in31(r31), .out(rs_data), .sel(rs));
  Multiplexer #(.select(5), .width(32)) multiplexer_2 (
    .in0(register_1_q), .in1(register_2_q), .in2(register_3_q), .in3(register_4_q), .in4(register_5_q),
    .in5(register_6_q), .in6(register_7_q), .in7(register_8_q), .in8(register_9_q), .in9(register_10_q),
    .in10(register_11_q), .in11(register_12_q), .in12(register_13_q), .in13(register_14_q),
    .in14(register_15_q), .in15(register_16_q), .in16(a), .in17(r17), .in18(r18), .in19(r19), .in20(r20),
    .in21(r21), .in22(r22), .in23(r23), .in24(r24), .in25(r25), .in26(r26), .in27(r27), .in28(r28),
    .in29(r29), .in30(r30), .in31(r31), .out(rt_data), .sel(rt));

  // Other names for the same wires on the sheet: multRS[31:0] = rs_data; multRT[31:0] = rt_data; r16[31:0] = a;
  //   WE_IN = write_e
endmodule

module ALU (
  input  [31:0] OP1,
  input  [31:0] OP2,
  input  [4:0] ALU_CODE,
  output [31:0] Res
);

  wire clock_1_out, comparator_1_lt, comparator_2_eq, comparator_3_eq, comparator_4_eq, comparator_5_eq,
       comparator_6_eq, comparator_7_eq, or_2_out, or_3_out;
  wire [4:0] bit_extender_1_out;
  wire [31:0] adder_1_out, and_1_out, bit_extender_2_out, bit_extender_3_out, divider_1_out, divider_1_rem,
       HI_q, LO_q, multiplexer_1_out, multiplexer_2_out, multiplexer_3_out, multiplier_1_cout,
       multiplier_1_out, not_1_out, or_1_out, shifter_1_out, shifter_2_out, subtractor_1_out, xor_1_out;

  Bit_Extender #(.in_width(32), .out_width(5)) bit_extender_1 (.in(OP2), .out(bit_extender_1_out));
  Comparator #(.width(32)) comparator_1 (.a(OP1), .b(OP2), .lt(comparator_1_lt));  // open: gt, eq
  assign and_1_out = OP1 & OP2;  // AND_Gate and_1, 32 bits wide
  assign xor_1_out = OP1 ^ OP2;  // XOR_Gate xor_1, 32 bits wide
  Adder #(.width(32)) adder_1 (.a(OP1), .b(OP2), .out(adder_1_out));  // open: cin, cout
  Subtractor #(.width(32)) subtractor_1 (.a(OP1), .b(OP2), .out(subtractor_1_out));  // open: bin, bout
  Multiplier #(.width(32)) multiplier_1 (
    .a(OP1), .b(OP2), .out(multiplier_1_out), .cout(multiplier_1_cout));  // open: cin
  Divider #(.width(32)) divider_1 (.a(OP1), .b(OP2), .out(divider_1_out), .rem(divider_1_rem));  // open: upper
  assign bit_extender_2_out = {{31{1'b0}}, comparator_1_lt};  // Bit_Extender bit_extender_2
  Shifter #(.width(32)) shifter_1 (.in(OP1), .\dist (bit_extender_1_out), .out(shifter_1_out));
  Shifter #(.shift("lr"), .width(32)) shifter_2 (.in(OP1), .\dist (bit_extender_1_out), .out(shifter_2_out));
  Comparator #(.width(32)) comparator_2 (.a(OP1), .b(OP2), .eq(comparator_2_eq));  // open: gt, lt
  assign or_1_out = OP1 | OP2;  // OR_Gate or_1, 32 bits wide
  assign bit_extender_3_out = {{31{comparator_2_eq}}, comparator_2_eq};  // Bit_Extender bit_extender_3
  assign not_1_out = ~or_1_out;  // NOT_Gate not_1, 32 bits wide
  Comparator #(.width(5)) comparator_3 (.a(ALU_CODE), .b(5'b00101), .eq(comparator_3_eq));  // open: gt, lt
  Shifter #(.width(32)) shifter_3 (.\dist (5'b10000));  // open: in, out
  Multiplexer #(.width(32)) multiplexer_1 (
    .in0(multiplier_1_cout), .in1(divider_1_rem), .out(multiplexer_1_out), .sel(comparator_3_eq));
  Multiplexer #(.width(32)) multiplexer_2 (
    .in0(multiplier_1_out), .in1(divider_1_out), .out(multiplexer_2_out), .sel(comparator_3_eq));
  Clock clock_1 (.out(clock_1_out));
  Comparator #(.width(5)) comparator_4 (.a(ALU_CODE), .b(5'b00101), .eq(comparator_4_eq));  // open: gt, lt
  Comparator #(.width(5)) comparator_5 (.a(ALU_CODE), .b(5'b00100), .eq(comparator_5_eq));  // open: gt, lt
  Register #(.width(32)) HI (.D(multiplexer_1_out), .en(or_2_out), .clk(clock_1_out), .Q(HI_q));  // open: clr
  Register #(.width(32)) LO (.D(multiplexer_2_out), .en(or_2_out), .clk(clock_1_out), .Q(LO_q));  // open: clr
  or or_2 (or_2_out, comparator_4_eq, comparator_5_eq);
  Multiplexer #(.select(5), .width(32)) multiplexer_3 (
    .in0(adder_1_out), .in1(subtractor_1_out), .in2(HI_q), .in3(LO_q), .in6(bit_extender_2_out),
    .in7(shifter_1_out), .in8(shifter_2_out), .in9(OP2), .in10(or_1_out), .in11(bit_extender_3_out),
    .in12(and_1_out), .in13(or_1_out), .in14(xor_1_out), .in15(not_1_out), .out(multiplexer_3_out),
    .sel(ALU_CODE));  // open: in4, in5, in16, in17, in18, in19, in20, in21, in22, in23, in24, in25, in26, in27, in28, in29, in30, in31
  Comparator #(.width(5)) comparator_6 (.a(ALU_CODE), .b(5'b00100), .eq(comparator_6_eq));  // open: gt, lt
  Comparator #(.width(5)) comparator_7 (.a(ALU_CODE), .b(5'b00101), .eq(comparator_7_eq));  // open: gt, lt
  Multiplexer #(.width(32)) multiplexer_4 (.in0(multiplexer_3_out), .in1({32{1'b0}}), .out(Res), .sel(or_3_out));
  or or_3 (or_3_out, comparator_6_eq, comparator_7_eq);

  // Other names for the same wires on the sheet: al_in[4:0] = ALU_CODE
endmodule

module Control (
  input  [31:0] Inst,
  output imm_sel,
  output [4:0] rd,
  output [4:0] rs,
  output [31:0] imm,
  output reg_write_e,
  output [4:0] ALU_code,
  output [4:0] rt,
  output MemWE,
  output DataOutPlexer,
  output JALRJALSignal,
  output ALLJUMPSelect,
  output JumpJALSelect
);

  wire and_1_out, and_2_out, and_3_out, and_4_out, and_5_out, comparator_1_eq, comparator_2_eq,
       comparator_3_eq, comparator_4_eq, comparator_6_eq, comparator_9_eq, comparator_10_eq,
       comparator_11_eq, comparator_12_eq, comparator_13_eq, comparator_14_eq, comparator_16_eq,
       comparator_17_eq, comparator_18_eq, comparator_19_eq, comparator_20_eq, comparator_21_eq,
       comparator_22_eq, comparator_23_eq, not_1_out, not_2_out, or_1_out, or_4_out, or_6_out, or_7_out,
       or_9_out, or_10_out, Rtype, Syscall;
  wire [4:0] multiplexer_6_out, multiplexer_8_out, multiplexer_9_out;
  wire [5:0] funcode;
  wire [31:0] bit_extender_1_out, bit_extender_2_out, bit_extender_3_out, multiplexer_4_out,
       multiplexer_5_out, shifter_1_out;
  wire [31:6] multiplexer_1_out;

  Comparator #(.width(32)) comparator_1 (.a(Inst), .b(32'hd00c), .eq(comparator_1_eq));  // open: gt, lt
  Multiplexer #(.width(32)) multiplexer_1 (
    .in0(Inst), .in1(32'hd009), .out({multiplexer_1_out, funcode}), .sel(comparator_1_eq));
  Multiplexer #(.width(5)) multiplexer_2 (
    .in0(multiplexer_1_out[25:21]), .in1(multiplexer_1_out[20:16]), .out(rs), .sel(and_5_out));
  Comparator #(.width(6)) comparator_2 (
    .a(multiplexer_1_out[31:26]), .b(6'b001100), .eq(comparator_2_eq));  // open: gt, lt
  Comparator #(.width(6)) comparator_3 (
    .a(multiplexer_1_out[31:26]), .b(6'b001101), .eq(comparator_3_eq));  // open: gt, lt
  Comparator #(.width(6)) comparator_4 (
    .a(multiplexer_1_out[31:26]), .b(6'b001110), .eq(comparator_4_eq));  // open: gt, lt
  Comparator #(.width(6)) comparator_5 (.a(multiplexer_1_out[31:26]), .b({6{1'b0}}), .eq(Rtype));  // open: gt, lt
  assign bit_extender_1_out = {{16{multiplexer_1_out[15]}}, {multiplexer_1_out[15:6], funcode}};  // Bit_Extender bit_extender_1
  assign bit_extender_2_out = {{16{1'b0}}, {multiplexer_1_out[15:6], funcode}};  // Bit_Extender bit_extender_2
  or or_1 (or_1_out, comparator_2_eq, comparator_3_eq, comparator_4_eq);
  not not_1 (not_1_out, Rtype);
  Multiplexer #(.width(5)) multiplexer_3 (.in0(multiplexer_1_out[20:16]), .in1({5{1'b0}}), .out(rt), .sel(or_10_out));
  Shifter #(.width(32)) shifter_1 (.in(bit_extender_2_out), .\dist (5'b10000), .out(shifter_1_out));
  Multiplexer #(.width(32)) multiplexer_4 (
    .in0(bit_extender_1_out), .in1(bit_extender_2_out), .out(multiplexer_4_out), .sel(or_1_out));
  or or_2 (imm_sel, not_1_out, and_5_out);
  Multiplexer #(.width(32)) multiplexer_5 (
    .in0(multiplexer_4_out), .in1(shifter_1_out), .out(multiplexer_5_out), .sel(comparator_6_eq));
  Comparator #(.width(6)) comparator_6 (
    .a(multiplexer_1_out[31:26]), .b(6'b001111), .eq(comparator_6_eq));  // open: gt, lt
  Comparator #(.width(6)) comparator_7 (.a(multiplexer_1_out[31:26]), .b(6'b101011), .eq(MemWE));  // open: gt, lt
  Comparator #(.width(6)) comparator_8 (
    .a(multiplexer_1_out[31:26]), .b(6'b100011), .eq(DataOutPlexer));  // open: gt, lt
  Comparator #(.width(6)) comparator_9 (.a(funcode), .b(6'b001001), .eq(comparator_9_eq));  // open: gt, lt
  Comparator #(.width(6)) comparator_10 (
    .a(multiplexer_1_out[31:26]), .b(6'b000011), .eq(comparator_10_eq));  // open: gt, lt
  Comparator #(.width(6)) comparator_11 (
    .a(multiplexer_1_out[31:26]), .b(6'b001000), .eq(comparator_11_eq));  // open: gt, lt
  Comparator #(.width(6)) comparator_12 (
    .a(multiplexer_1_out[31:26]), .b(6'b100011), .eq(comparator_12_eq));  // open: gt, lt
  ALUCodeAssigner alucodeassigner_1 (.OpCode(multiplexer_1_out[31:26]), .FuncCode(funcode), .ALU_Code(ALU_code));
  or or_3 (JALRJALSignal, and_1_out, comparator_10_eq);
  Comparator #(.width(6)) comparator_13 (.a(funcode), .b(6'b001000), .eq(comparator_13_eq));  // open: gt, lt
  Comparator #(.width(6)) comparator_14 (
    .a(multiplexer_1_out[31:26]), .b(6'b000010), .eq(comparator_14_eq));  // open: gt, lt
  OPcodeComparerWE opcodecomparerwe_1 (.OP(multiplexer_1_out[31:26]), .FUNC(funcode), .WE(reg_write_e));
  and and_1 (and_1_out, Rtype, comparator_9_eq);
  and and_2 (and_2_out, Rtype, comparator_13_eq);
  or or_4 (or_4_out, and_2_out, comparator_14_eq);
  or or_5 (JumpJALSelect, comparator_10_eq, comparator_14_eq);
  Comparator #(.width(6)) comparator_15 (.a(multiplexer_1_out[31:26]), .b(6'b001100), .eq(Syscall));  // open: gt, lt
  Multiplexer #(.width(5)) multiplexer_6 (
    .in0(multiplexer_1_out[15:11]), .in1(multiplexer_1_out[20:16]), .out(multiplexer_6_out), .sel(or_6_out));
  or or_6 (or_6_out, comparator_11_eq, comparator_12_eq);
  Multiplexer #(.width(5)) multiplexer_7 (
    .in0(multiplexer_9_out), .in1(multiplexer_1_out[20:16]), .out(rd), .sel(or_10_out));
  or or_7 (or_7_out, JALRJALSignal, or_4_out);
  Multiplexer #(.width(5)) multiplexer_8 (
    .in0(multiplexer_6_out), .in1(5'b11010), .out(multiplexer_8_out), .sel(Syscall));
  Comparator #(.width(5)) comparator_16 (
    .a(multiplexer_1_out[15:11]), .b(5'b11010), .eq(comparator_16_eq));  // open: gt, lt
  Multiplexer #(.width(5)) multiplexer_9 (
    .in0(multiplexer_8_out), .in1({5{1'b1}}), .out(multiplexer_9_out), .sel(and_3_out));
  not not_2 (not_2_out, comparator_16_eq);
  Comparator #(.width(6)) comparator_17 (.a(funcode), .b(6'b000010), .eq(comparator_17_eq));  // open: gt, lt
  Comparator #(.width(6)) comparator_18 (.a(funcode), .b({6{1'b0}}), .eq(comparator_18_eq));  // open: gt, lt
  or or_8 (ALLJUMPSelect, or_7_out, Syscall);
  and and_3 (and_3_out, not_2_out, JALRJALSignal);
  and and_4 (and_4_out, Rtype, or_9_out);
  or or_9 (or_9_out, comparator_17_eq, comparator_18_eq);
  Comparator #(.width(6)) comparator_19 (
    .a(multiplexer_1_out[31:26]), .b({6{1'b0}}), .eq(comparator_19_eq));  // open: gt, lt
  Comparator #(.width(6)) comparator_20 (
    .a(multiplexer_1_out[31:26]), .b(6'b001100), .eq(comparator_20_eq));  // open: gt, lt
  Comparator #(.width(6)) comparator_21 (
    .a(multiplexer_1_out[31:26]), .b(6'b001101), .eq(comparator_21_eq));  // open: gt, lt
  Comparator #(.width(6)) comparator_22 (
    .a(multiplexer_1_out[31:26]), .b(6'b001110), .eq(comparator_22_eq));  // open: gt, lt
  Comparator #(.width(6)) comparator_23 (
    .a(multiplexer_1_out[31:26]), .b(6'b001111), .eq(comparator_23_eq));  // open: gt, lt
  assign bit_extender_3_out = {{27{1'b0}}, multiplexer_1_out[10:6]};  // Bit_Extender bit_extender_3
  and and_5 (and_5_out, and_4_out, comparator_19_eq);
  or or_10 (or_10_out, comparator_20_eq, comparator_21_eq, comparator_23_eq, comparator_22_eq);
  Multiplexer #(.width(32)) multiplexer_10 (
    .in0(multiplexer_5_out), .in1(bit_extender_3_out), .out(imm), .sel(and_5_out));

  // Notes on the sheet:
  //   FUNCCODE
  //   SHAMT
  //   RD
  //   RT
  //   RS
  //   OPCODE
  //   Checks if R type, if opcode is 0 then instruction is R type if not I type
  //   Handling how immediates should be extended
  //   Putting Shamt into rt 
  //   OPcode==11 OR Funccode=9
  //   Replace RD sel with RT for ori,lui,andi.xori
endmodule

module OPcodeComparerWE (
  input  [5:0] OP,
  input  [5:0] FUNC,
  output WE
);

  wire comparator_1_eq, comparator_2_eq, comparator_3_eq, comparator_4_eq, comparator_5_eq, comparator_6_eq,
       comparator_7_eq, comparator_8_eq, comparator_9_eq, multiplexer_1_out, or_1_out, or_2_out;

  Comparator #(.width(6)) comparator_1 (.a(FUNC), .b(6'b001000), .eq(comparator_1_eq));  // open: gt, lt
  Comparator #(.width(6)) comparator_2 (.a(FUNC), .b(6'b011000), .eq(comparator_2_eq));  // open: gt, lt
  Comparator #(.width(6)) comparator_3 (.a(FUNC), .b(6'b011010), .eq(comparator_3_eq));  // open: gt, lt
  or or_1 (or_1_out, comparator_1_eq, comparator_2_eq, comparator_3_eq);
  Comparator #(.width(6)) comparator_4 (.a(OP), .b(6'b000010), .eq(comparator_4_eq));  // open: gt, lt
  Comparator #(.width(6)) comparator_5 (.a(OP), .b(6'b000100), .eq(comparator_5_eq));  // open: gt, lt
  Comparator #(.width(6)) comparator_6 (.a(OP), .b(6'b000101), .eq(comparator_6_eq));  // open: gt, lt
  Comparator #(.width(6)) comparator_7 (.a(OP), .b(6'b001100), .eq(comparator_7_eq));  // open: gt, lt
  Comparator #(.width(6)) comparator_8 (.a(OP), .b(6'b101011), .eq(comparator_8_eq));  // open: gt, lt
  Comparator #(.width(6)) comparator_9 (.a(OP), .b({6{1'b0}}), .eq(comparator_9_eq));  // open: gt, lt
  or or_2 (or_2_out, comparator_4_eq, comparator_5_eq, comparator_6_eq, comparator_7_eq, comparator_8_eq);
  Multiplexer multiplexer_1 (.in0(or_2_out), .in1(or_1_out), .out(multiplexer_1_out), .sel(comparator_9_eq));
  not not_1 (WE, multiplexer_1_out);

  // Notes on the sheet:
  //   Done by referencing our truth table
  //   Less instructions have WE off so we will check for which ones dont need WE in this circuit
  //   If func code is 8, 24,26 then WE off
  //   we will check if 2,4,5,12,43 OP codes are present and if so those are the ones were WE is off
  //   If opCode is 0 then we use output from logic based on func code
  //   Negated as we are checking if WE is off and this cicuit should output if it is on
endmodule

module ALUCodeAssigner (
  input  [5:0] OpCode,
  input  [5:0] FuncCode,
  output [4:0] ALU_Code
);

  wire comparator_2_eq, comparator_3_eq, comparator_4_eq, comparator_5_eq, comparator_6_eq, comparator_7_eq,
       comparator_8_eq, comparator_9_eq, comparator_10_eq, comparator_11_eq, comparator_12_eq,
       comparator_13_eq, comparator_14_eq, comparator_15_eq, comparator_16_eq, comparator_17_eq,
       comparator_18_eq, comparator_19_eq, comparator_20_eq, comparator_21_eq, comparator_22_eq,
       comparator_23_eq, mult1, priority_encoder_1_en_out, priority_encoder_2_en_out;
  wire [3:0] multiplexer_1_out, multiplexer_2_out, priority_encoder_1_out, priority_encoder_2_out;
  wire [4:0] multiplexer_3_out, multiplexer_4_out;

  Comparator #(.width(6)) comparator_1 (.a(OpCode), .b({6{1'b0}}), .eq(mult1));  // open: gt, lt
  Comparator #(.width(6)) comparator_2 (.a(FuncCode), .b(6'b100000), .eq(comparator_2_eq));  // open: gt, lt
  Comparator #(.width(6)) comparator_3 (.a(FuncCode), .b(6'b100010), .eq(comparator_3_eq));  // open: gt, lt
  Comparator #(.width(6)) comparator_4 (.a(FuncCode), .b(6'b010000), .eq(comparator_4_eq));  // open: gt, lt
  Comparator #(.width(6)) comparator_5 (.a(FuncCode), .b(6'b010010), .eq(comparator_5_eq));  // open: gt, lt
  Comparator #(.width(6)) comparator_6 (.a(FuncCode), .b(6'b011000), .eq(comparator_6_eq));  // open: gt, lt
  Comparator #(.width(6)) comparator_7 (.a(FuncCode), .b(6'b011010), .eq(comparator_7_eq));  // open: gt, lt
  Comparator #(.width(6)) comparator_8 (.a(FuncCode), .b(6'b101010), .eq(comparator_8_eq));  // open: gt, lt
  Comparator #(.width(6)) comparator_9 (.a(FuncCode), .b({6{1'b0}}), .eq(comparator_9_eq));  // open: gt, lt
  Comparator #(.width(6)) comparator_10 (.a(FuncCode), .b(6'b000010), .eq(comparator_10_eq));  // open: gt, lt
  Comparator #(.width(6)) comparator_11 (.a(FuncCode), .b(6'b100100), .eq(comparator_11_eq));  // open: gt, lt
  Comparator #(.width(6)) comparator_12 (.a(FuncCode), .b(6'b100101), .eq(comparator_12_eq));  // open: gt, lt
  Comparator #(.width(6)) comparator_13 (.a(FuncCode), .b(6'b100110), .eq(comparator_13_eq));  // open: gt, lt
  Comparator #(.width(6)) comparator_14 (.a(FuncCode), .b(6'b100111), .eq(comparator_14_eq));  // open: gt, lt
  Comparator #(.width(6)) comparator_15 (.a(OpCode), .b(6'b001000), .eq(comparator_15_eq));  // open: gt, lt
  Comparator #(.width(6)) comparator_16 (.a(OpCode), .b(6'b100011), .eq(comparator_16_eq));  // open: gt, lt
  Comparator #(.width(6)) comparator_17 (.a(OpCode), .b(6'b101011), .eq(comparator_17_eq));  // open: gt, lt
  Comparator #(.width(6)) comparator_18 (.a(OpCode), .b(6'b001111), .eq(comparator_18_eq));  // open: gt, lt
  Comparator #(.width(6)) comparator_19 (.a(OpCode), .b(6'b001101), .eq(comparator_19_eq));  // open: gt, lt
  Comparator #(.width(6)) comparator_20 (.a(OpCode), .b(6'b000100), .eq(comparator_20_eq));  // open: gt, lt
  Comparator #(.width(6)) comparator_21 (.a(OpCode), .b(6'b000101), .eq(comparator_21_eq));  // open: gt, lt
  Comparator #(.width(6)) comparator_22 (.a(OpCode), .b(6'b001100), .eq(comparator_22_eq));  // open: gt, lt
  Comparator #(.width(6)) comparator_23 (.a(OpCode), .b(6'b001110), .eq(comparator_23_eq));  // open: gt, lt
  Priority_Encoder #(.select(4)) priority_encoder_1 (
    .in0(comparator_2_eq), .in1(comparator_3_eq), .in2(comparator_4_eq), .in3(comparator_5_eq),
    .in4(comparator_6_eq), .in5(comparator_7_eq), .in6(comparator_8_eq), .in7(comparator_9_eq),
    .in8(comparator_10_eq), .in9(comparator_11_eq), .in10(comparator_12_eq), .in11(comparator_13_eq),
    .in12(comparator_14_eq), .out(priority_encoder_1_out), .en_out(priority_encoder_1_en_out));  // open: in13, in14, in15, gs, en_in
  Priority_Encoder #(.select(4)) priority_encoder_2 (
    .in0(comparator_15_eq), .in1(comparator_16_eq), .in2(comparator_17_eq), .in3(comparator_18_eq),
    .in4(comparator_19_eq), .in5(comparator_20_eq), .in6(comparator_21_eq), .in7(comparator_22_eq),
    .in8(comparator_23_eq), .out(priority_encoder_2_out), .en_out(priority_encoder_2_en_out));  // open: in9, in10, in11, in12, in13, in14, in15, gs, en_in
  Multiplexer #(.width(4)) multiplexer_1 (
    .in0(priority_encoder_1_out), .in1(4'b0000), .out(multiplexer_1_out), .sel(priority_encoder_1_en_out));
  Multiplexer #(.width(4)) multiplexer_2 (
    .in0(priority_encoder_2_out), .in1(4'b0000), .out(multiplexer_2_out), .sel(priority_encoder_2_en_out));
  Multiplexer #(.select(4), .width(5)) multiplexer_3 (
    .in0({5{1'b0}}), .in1(5'b00001), .in2(5'b00010), .in3(5'b00011), .in4(5'b00100), .in5(5'b00101),
    .in6(5'b00110), .in7(5'b00111), .in8(5'b01000), .in9(5'b01100), .in10(5'b01101), .in11(5'b01110),
    .in12(5'b01111), .out(multiplexer_3_out), .sel(multiplexer_1_out));  // open: in13, in14, in15
  Multiplexer #(.select(4), .width(5)) multiplexer_4 (
    .in0({5{1'b0}}), .in1({5{1'b0}}), .in2({5{1'b0}}), .in3(5'b01001), .in4(5'b01010), .in5(5'b01011),
    .in6(5'b01100), .in7(5'b01110), .out(multiplexer_4_out), .sel(multiplexer_2_out));  // open: in8, in9, in10, in11, in12, in13, in14, in15
  Multiplexer #(.width(5)) multiplexer_5 (
    .in0(multiplexer_4_out), .in1(multiplexer_3_out), .out(ALU_Code), .sel(mult1));

  // Notes on the sheet:
  //   If opCode is 0 then all information needed is stored in funcCode (R type)
  //   ADD
  //   SUB
  //   MFHI
  //   MFLO
  //   MULT
  //   DIV
  //   SLT
  //   SLL
  //   SRL
  //   AND
  //   OR
  //   XOR
  //   NOR
  //   ADDI
  //   LW
  //   SW
  //   LUI
  //   ORI
  //   BEQ
  //   BNE
  //   ANDI
  //   XORI
  //   To stop errors when Jumps
  //   To stop errors when Jumps
endmodule

module BranchCheck (
  input  [5:0] Opcode,
  input  isEqual,
  output IsBranch
);

  wire and_1_out, and_2_out, comparator_1_eq, comparator_2_eq, not_1_out;

  Comparator #(.width(6)) comparator_1 (.a(Opcode), .b(6'b000100), .eq(comparator_1_eq));  // open: gt, lt
  Comparator #(.width(6)) comparator_2 (.a(Opcode), .b(6'b000101), .eq(comparator_2_eq));  // open: gt, lt
  not not_1 (not_1_out, isEqual);
  and and_1 (and_1_out, comparator_1_eq, isEqual);
  and and_2 (and_2_out, comparator_2_eq, not_1_out);
  or or_1 (IsBranch, and_1_out, and_2_out);
endmodule

module JoyStickController (
  input  [31:0] DataFromBus,
  input  WriteEnableFromBus,
  input  [31:0] AddressFromBus,
  input  [3:0] JoyStickDataX,
  input  [3:0] JoyStickDataY,
  output WriteToBus,
  output [31:0] DataToBus
);

  wire comparator_1_eq, comparator_2_eq, not_1_out, or_1_out;
  wire [31:0] bit_extender_1_out, bit_extender_2_out;

  not not_1 (not_1_out, WriteEnableFromBus);
  assign bit_extender_1_out = {{28{1'b0}}, JoyStickDataX};  // Bit_Extender bit_extender_1
  assign bit_extender_2_out = {{28{1'b0}}, JoyStickDataY};  // Bit_Extender bit_extender_2
  Comparator #(.mode("unsigned"), .width(32)) comparator_1 (
    .a(AddressFromBus), .b(32'hfffff030), .eq(comparator_1_eq));  // open: gt, lt
  Comparator #(.mode("unsigned"), .width(32)) comparator_2 (
    .a(AddressFromBus), .b(32'hfffff034), .eq(comparator_2_eq));  // open: gt, lt
  or or_1 (or_1_out, comparator_1_eq, comparator_2_eq);
  Multiplexer #(.width(32)) multiplexer_1 (
    .in0(bit_extender_1_out), .in1(bit_extender_2_out), .out(DataToBus), .sel(comparator_2_eq));
  and and_1 (WriteToBus, or_1_out, not_1_out);

  // Notes on the sheet:
  //   On 030 we write X cord to bus
  //   On 034 we write Y cord to bus
endmodule

module SliderController (
  input  WriteEnableFromBus,
  input  [31:0] AddressFromBus,
  input  [7:0] SliderData,
  output WriteToBus,
  output [31:0] DataToBus
);

  wire comparator_1_eq, not_1_out;

  Comparator #(.mode("unsigned"), .width(32)) comparator_1 (
    .a(AddressFromBus), .b(32'hfffff038), .eq(comparator_1_eq));  // open: gt, lt
  assign DataToBus = {{24{1'b0}}, SliderData};  // Bit_Extender bit_extender_1
  not not_1 (not_1_out, WriteEnableFromBus);
  and and_1 (WriteToBus, not_1_out, comparator_1_eq);
endmodule

module LEDHexController (
  input  WriteEnableFromBus,
  input  [31:0] AddressFromBus,
  input  [31:0] DataFromBus,
  output [3:0] DataToLED
);

  wire and_1_out, clock_1_out, comparator_1_eq;
  wire [3:0] bit_extender_1_out;

  Bit_Extender #(.in_width(32), .out_width(4), .\type ("zero")) bit_extender_1 (
    .in(DataFromBus), .out(bit_extender_1_out));
  Comparator #(.mode("unsigned"), .width(32)) comparator_1 (
    .a(AddressFromBus), .b(32'hfffff03c), .eq(comparator_1_eq));  // open: gt, lt
  and and_1 (and_1_out, WriteEnableFromBus, comparator_1_eq);
  Register #(.width(4)) register_1 (
    .D(bit_extender_1_out), .en(and_1_out), .clk(clock_1_out), .Q(DataToLED));  // open: clr
  Clock clock_1 (.out(clock_1_out));

  // Notes on the sheet:
  //   Implemented where it will write to the hex LED and keep that value until the next time it is written to
endmodule

module BuzzerController (
  input  [31:0] AddressFromBus,
  input  [31:0] DataFromBus,
  input  WriteEnable,
  output [6:0] VolOut,
  output [13:0] FreqOut,
  output [7:0] DutyCycleOut,
  output BuzzerOn
);

  wire and_1_out, and_2_out, and_3_out, clock_1_out, comparator_1_eq, comparator_2_eq, comparator_3_eq,
       comparator_4_eq;
  wire [6:0] bit_extender_1_out;
  wire [7:0] bit_extender_3_out;
  wire [13:0] bit_extender_2_out;

  Bit_Extender #(.in_width(32), .out_width(7), .\type ("zero")) bit_extender_1 (
    .in(DataFromBus), .out(bit_extender_1_out));
  Bit_Extender #(.in_width(32), .out_width(14), .\type ("zero")) bit_extender_2 (
    .in(DataFromBus), .out(bit_extender_2_out));
  Bit_Extender #(.in_width(32), .out_width(8), .\type ("zero")) bit_extender_3 (
    .in(DataFromBus), .out(bit_extender_3_out));
  Comparator #(.mode("unsigned"), .width(32)) comparator_1 (
    .a(AddressFromBus), .b(32'hfffff040), .eq(comparator_1_eq));  // open: gt, lt
  Comparator #(.mode("unsigned"), .width(32)) comparator_2 (
    .a(AddressFromBus), .b(32'hfffff044), .eq(comparator_2_eq));  // open: gt, lt
  Comparator #(.mode("unsigned"), .width(32)) comparator_3 (
    .a(AddressFromBus), .b(32'hfffff048), .eq(comparator_3_eq));  // open: gt, lt
  Comparator #(.mode("unsigned"), .width(32)) comparator_4 (
    .a(AddressFromBus), .b(32'hfffff04c), .eq(comparator_4_eq));  // open: gt, lt
  Clock clock_1 (.out(clock_1_out));
  and and_1 (and_1_out, WriteEnable, comparator_1_eq);
  and and_2 (and_2_out, WriteEnable, comparator_2_eq);
  and and_3 (and_3_out, WriteEnable, comparator_3_eq);
  and and_4 (BuzzerOn, WriteEnable, comparator_4_eq);
  Register #(.width(7)) Volume (.D(bit_extender_1_out), .en(and_1_out), .clk(clock_1_out), .Q(VolOut));  // open: clr
  Register #(.width(14)) Frequency (
    .D(bit_extender_2_out), .en(and_2_out), .clk(clock_1_out), .Q(FreqOut));  // open: clr
  Register DutyCycle (.D(bit_extender_3_out), .en(and_3_out), .clk(clock_1_out), .Q(DutyCycleOut));  // open: clr

  // Notes on the sheet:
  //   We use sw to write to intenral registers and then turn on with 04c
endmodule
